// Logisim project CPU.circ as structural Verilog: 1 circuit, main circuit main
module main (
);

  wire and_1_out, and_2_out, and_3_out, and_4_out, and_5_out, and_7_out, Bit1, Bit2, Bit3, Bit4, Bit5, Bit6,
       Bit7, Bit8, Bit9, Bit10, Bit11, Bit12, Bit13, Bit14, Bit15, Bit16, ClockSync, comparator_2_eq,
       isExecute, isMovInstruction, isMovRegA, not_1_out, not_2_out, not_3_out, not_4_out, toExecute;
  wire [13:0] Operand1Data, Operand2Data;
  wire [14:0] InstructionData;
  wire [15:0] CounterValue, LDCounter;
  wire [63:0] register_2_q, register_3_q, register_4_q;
  wire [63:1] RAMData;

  Clock clock_1 (.out(ClockSync));
  Counter #(.max('hffff), .width(16)) counter_1 (
    .count(ClockSync), .clk(ClockSync), .D(LDCounter), .Q(CounterValue));  // open: clr, load, up, carry
  Register #(.width(14)) register_1 (.D(Operand2Data), .en(isMovRegA), .clk(ClockSync));  // open: Q, clr
  RAM #(.addrWidth(16), .dataWidth(64)) ram_1 (
    .addr(CounterValue), .clk(ClockSync),
    .dout({RAMData[63:61], Bit16, RAMData[59:57], Bit15, RAMData[55:53], Bit14, RAMData[51:49], Bit13, RAMData[47:45], Bit12, RAMData[43:41], Bit11, RAMData[39:37], Bit10, RAMData[35:33], Bit9, RAMData[31:29], Bit8, RAMData[27:25], Bit7, RAMData[23:21], Bit6, RAMData[19:17], Bit5, RAMData[15:13], Bit4, RAMData[11:9], Bit3, RAMData[7:5], Bit2, RAMData[3:1], Bit1}));  // open: we, oe, din
  not not_1 (not_1_out, toExecute);
  not not_2 (not_2_out, toExecute);
  and and_1 (and_1_out, Bit1, Bit2);
  not not_3 (not_3_out, and_1_out);
  not not_4 (not_4_out, toExecute);
  and and_2 (and_2_out, Bit1, Bit2);
  and and_3 (and_3_out, Bit1, not_1_out);
  and and_4 (and_4_out, not_2_out, not_3_out);
  and and_5 (and_5_out, not_4_out, and_2_out);
  Register #(.width(64)) register_2 (
    .D({RAMData[63:61], Bit16, RAMData[59:57], Bit15, RAMData[55:53], Bit14, RAMData[51:49], Bit13, RAMData[47:45], Bit12, RAMData[43:41], Bit11, RAMData[39:37], Bit10, RAMData[35:33], Bit9, RAMData[31:29], Bit8, RAMData[27:25], Bit7, RAMData[23:21], Bit6, RAMData[19:17], Bit5, RAMData[15:13], Bit4, RAMData[11:9], Bit3, RAMData[7:5], Bit2, RAMData[3:1], Bit1}),
    .en(and_3_out), .clk(ClockSync),
    .Q({register_2_q[63:61], InstructionData[14], register_2_q[59:57], InstructionData[13], register_2_q[55:53], InstructionData[12], register_2_q[51:49], InstructionData[11], register_2_q[47:45], InstructionData[10], register_2_q[43:41], InstructionData[9], register_2_q[39:37], InstructionData[8], register_2_q[35:33], InstructionData[7], register_2_q[31:29], InstructionData[6], register_2_q[27:25], InstructionData[5], register_2_q[23:21], InstructionData[4], register_2_q[19:17], InstructionData[3], register_2_q[15:13], InstructionData[2], register_2_q[11:9], InstructionData[1], register_2_q[7:5], InstructionData[0], register_2_q[3:0]}));  // open: clr
  Comparator #(.mode("unsigned"), .width(15)) comparator_1 (
    .a(InstructionData), .b(15'h1), .eq(isMovInstruction));  // open: gt, lt
  Register #(.width(64)) register_3 (
    .D({RAMData[63:61], Bit16, RAMData[59:57], Bit15, RAMData[55:53], Bit14, RAMData[51:49], Bit13, RAMData[47:45], Bit12, RAMData[43:41], Bit11, RAMData[39:37], Bit10, RAMData[35:33], Bit9, RAMData[31:29], Bit8, RAMData[27:25], Bit7, RAMData[23:21], Bit6, RAMData[19:17], Bit5, RAMData[15:13], Bit4, RAMData[11:9], Bit3, RAMData[7:5], Bit2, RAMData[3:1], Bit1}),
    .clk(ClockSync),
    .Q({register_3_q[63:61], Operand1Data[13], register_3_q[59:57], Operand1Data[12], register_3_q[55:53], Operand1Data[11], register_3_q[51:49], Operand1Data[10], register_3_q[47:45], Operand1Data[9], register_3_q[43:41], Operand1Data[8], register_3_q[39:37], Operand1Data[7], register_3_q[35:33], Operand1Data[6], register_3_q[31:29], Operand1Data[5], register_3_q[27:25], Operand1Data[4], register_3_q[23:21], Operand1Data[3], register_3_q[19:17], Operand1Data[2], register_3_q[15:13], Operand1Data[1], register_3_q[11:9], Operand1Data[0], register_3_q[7:0]}));  // open: en, clr
  Register #(.width(64)) register_4 (
    .D({RAMData[63:61], Bit16, RAMData[59:57], Bit15, RAMData[55:53], Bit14, RAMData[51:49], Bit13, RAMData[47:45], Bit12, RAMData[43:41], Bit11, RAMData[39:37], Bit10, RAMData[35:33], Bit9, RAMData[31:29], Bit8, RAMData[27:25], Bit7, RAMData[23:21], Bit6, RAMData[19:17], Bit5, RAMData[15:13], Bit4, RAMData[11:9], Bit3, RAMData[7:5], Bit2, RAMData[3:1], Bit1}),
    .en(and_5_out), .clk(ClockSync),
    .Q({register_4_q[63:61], Operand2Data[13], register_4_q[59:57], Operand2Data[12], register_4_q[55:53], Operand2Data[11], register_4_q[51:49], Operand2Data[10], register_4_q[47:45], Operand2Data[9], register_4_q[43:41], Operand2Data[8], register_4_q[39:37], Operand2Data[7], register_4_q[35:33], Operand2Data[6], register_4_q[31:29], Operand2Data[5], register_4_q[27:25], Operand2Data[4], register_4_q[23:21], Operand2Data[3], register_4_q[19:17], Operand2Data[2], register_4_q[15:13], Operand2Data[1], register_4_q[11:9], Operand2Data[0], register_4_q[7:0]}));  // open: clr
  Comparator #(.mode("unsigned"), .width(14)) comparator_2 (
    .a(Operand1Data), .b(14'h1), .eq(comparator_2_eq));  // open: gt, lt
  Comparator #(.mode("unsigned"), .width(64)) comparator_3 (
    .a({RAMData[63:61], Bit16, RAMData[59:57], Bit15, RAMData[55:53], Bit14, RAMData[51:49], Bit13, RAMData[47:45], Bit12, RAMData[43:41], Bit11, RAMData[39:37], Bit10, RAMData[35:33], Bit9, RAMData[31:29], Bit8, RAMData[27:25], Bit7, RAMData[23:21], Bit6, RAMData[19:17], Bit5, RAMData[15:13], Bit4, RAMData[11:9], Bit3, RAMData[7:5], Bit2, RAMData[3:1], Bit1}),
    .b({64{1'b1}}), .eq(isExecute));  // open: gt, lt
  and and_6 (isMovRegA, comparator_2_eq, isMovInstruction);
  and and_7 (and_7_out, ClockSync, isExecute);
  and and_8 (toExecute, and_7_out, isMovInstruction);

  // Other names for the same wires on the sheet: RAMData (some bits) = {Bit16, Bit15, Bit14, Bit13, Bit12, Bit11, Bit10, Bit9, Bit8, Bit7, Bit6, Bit5, Bit4, Bit3, Bit2, Bit1}

  // Notes on the sheet:
  //   Clock
  //   Fetch Unit
  //   Program Counter
  //   DataBus
  //   Instruction Register
  //   Opcode Register 1
  //   Opcode Register 1
  //   Decode Unit
  //   Execution Unit
endmodule
